# Fritzing sketch bme280 (saved by Fritzing 0.9.10b)
breadboards: 1

parts:
  U1 = ESP32-38PinWide [part_number=ESP32-38PinWide]
  Part1 = BME280 Breakout

nets:
  N1: U1.3.3, Part1.3.3V
  N2: U1.GPIO25, Part1.SCK/SCL
  N3: U1.GPIO26, Part1.SDI/SDA
  GND: U1.GND, Part1.GND

custom parts:
  ESP32-38PinWide: Generic 38-Pin ESP32 with wide format (only access to one side of pins on a breadboard) based on Stephen Lilley's HiLetgo ESP-WROOM-32 ESP32 ESP-32S Development Board.
