# Fritzing sketch buzzer (saved by Fritzing 0.9.10b)
breadboards: 1

parts:
  U1 = ESP32-38PinWide [part_number=ESP32-38PinWide]
  Grove1 = Grove Buzz

nets:
  N1: U1.3.3, Grove1.VCC
  N2: U1.GPIO14, Grove1.SIG
  GND: U1.GND, Grove1.GND

custom parts:
  ESP32-38PinWide: Generic 38-Pin ESP32 with wide format (only access to one side of pins on a breadboard) based on Stephen Lilley's HiLetgo ESP-WROOM-32 ESP32 ESP-32S Development Board.
