# Fritzing sketch ds18b20 (saved by Fritzing 0.9.10b)
breadboards: 1

parts:
  U1 = ESP32-38PinWide [part_number=ESP32-38PinWide]
  DS1 = DS18B20 1-Wire Temperature Sensor Module - 7 available pins [part_number=DS18B20]

nets:
  N1: U1.3.3, DS1.VCC
  N2: U1.GPIO32, DS1.DQ
  GND: U1.GND, DS1.GND

custom parts:
  ESP32-38PinWide: Generic 38-Pin ESP32 with wide format (only access to one side of pins on a breadboard) based on Stephen Lilley's HiLetgo ESP-WROOM-32 ESP32 ESP-32S Development Board.
  DS18B20 1-Wire Temperature Sensor Module - 7 available pins: DS18B20 1-Wire Temperature Sensor Module ************* This module includes 4,7kΩ resistor
