# Fritzing sketch leds (saved by Fritzing 0.9.10b)
breadboards: 1

parts:
  LED1 = smd LED [color="Red (633nm)" package="0603 [SMD]"]
  U1 = ESP32-38PinWide [part_number=ESP32-38PinWide]
  R1 = Resistor [tolerance=±5% power=0.25 resistance=330 package=THT]
  LED2 = smd LED [color="Green (565nm)" package="0603 [SMD]"]
  R2 = Resistor [tolerance=±5% power=0.25 resistance=330 package=THT]
  R3 = Resistor [tolerance=±5% power=0.25 resistance=330 package=THT]
  R4 = Resistor [tolerance=±5% power=0.25 resistance=330 package=THT]
  LED3 = smd LED [color="Red (633nm)" package="0603 [SMD]"]
  LED4 = smd LED [color="Green (565nm)" package="0603 [SMD]"]
  LED5 = smd LED [color="Red (633nm)" package="1206 [SMD]"]

nets:
  N1: LED1.cathode, U1.GND, LED2.cathode, LED3.cathode, LED4.cathode, LED5.cathode
  N2: LED1.anode, R1.Pin_0
  N3: U1.GPIO32, R1.Pin_1
  N4: U1.GPIO33, R2.Pin_1
  N5: U1.GPIO25, R3.Pin_1
  N6: U1.GPIO26, R4.Pin_1
  N7: LED2.anode, R2.Pin_0
  N8: R3.Pin_0, LED3.anode
  N9: R4.Pin_0, LED4.anode

notes:
  connect LEDs like this

custom parts:
  ESP32-38PinWide: Generic 38-Pin ESP32 with wide format (only access to one side of pins on a breadboard) based on Stephen Lilley's HiLetgo ESP-WROOM-32 ESP32 ESP-32S Development Board.
