# Fritzing sketch rotary (saved by Fritzing 1.0.5)
breadboards: 1

parts:
  U1 = ESP32-38PinWide [part_number=ESP32-38PinWide]
  RE1 = KY-040 Rotary encoder [package="Breakout board"]

nets:
  N1: U1.3.3, RE1.Vcc
  N2: U1.GPIO32, RE1.CLK
  N3: U1.GPIO33, RE1.DT
  N4: U1.GPIO25, RE1.SW
  GND: U1.GND, RE1.GND

custom parts:
  ESP32-38PinWide: Generic 38-Pin ESP32 with wide format (only access to one side of pins on a breadboard) based on Stephen Lilley's HiLetgo ESP-WROOM-32 ESP32 ESP-32S Development Board.
  KY-040 Rotary encoder: KY-040 Rotary Encoder with switch on breakout borad from AZ Delivery
