# Fritzing sketch servo (saved by Fritzing 0.9.10b)
breadboards: 1

parts:
  U1 = ESP32-38PinWide [part_number=ESP32-38PinWide]
  J1 = Basic Servo

nets:
  N1: U1.3.3, J1.vcc
  N2: U1.GPIO12, J1.pulse
  GND: U1.GND, J1.gnd

custom parts:
  ESP32-38PinWide: Generic 38-Pin ESP32 with wide format (only access to one side of pins on a breadboard) based on Stephen Lilley's HiLetgo ESP-WROOM-32 ESP32 ESP-32S Development Board.
