# Fritzing sketch ultra (saved by Fritzing 0.9.10b)
breadboards: 1

parts:
  U1 = ESP32-38PinWide [part_number=ESP32-38PinWide]
  HC-SR04_Sensor_1 = HC-SR04 Ultrasonic Distance Sensor
  LED1 = LED - 3mm [color="Red (633nm)" current=0.030 package="3 mm [THT]"]

nets:
  N1: U1.GPIO32, LED1.cathode
  N2: U1.GPIO33, HC-SR04_Sensor_1.TRIG
  GND: U1.GND, HC-SR04_Sensor_1.GND
  VIN: U1.VIN, HC-SR04_Sensor_1.VCC
  N3: HC-SR04_Sensor_1.ECHO, LED1.anode

custom parts:
  ESP32-38PinWide: Generic 38-Pin ESP32 with wide format (only access to one side of pins on a breadboard) based on Stephen Lilley's HiLetgo ESP-WROOM-32 ESP32 ESP-32S Development Board.
